# Fritzing sketch Boat_schematic_rigtigt (saved by Fritzing 1.0.3b)
breadboards: 1

parts:
  3S_LiPo = DC Power [voltage=11.1V internal_resistance=0.1Ω]
  ESC_2 = Littlebee 30A ESC
  ESC_1 = Littlebee 30A ESC
  Arduino_Mega = Arduino Mega 2560 (Rev3)
  microSD = MicroSD Card Module
  U1 = ACS712 [package=so08]
  ESP = Amica NodeMCU DEVKIT 1.0
  Thruster_left = Basic Servo
  Thruster_right = Basic Servo
  LED_red = LED - 5mm [color="Red (633nm)" current=0.030A package="5 mm [THT]"]
  LED_green = LED - 5mm [color="Red (633nm)" current=30mA package="5 mm [THT]"]
  LED_blue = LED - 5mm [color="Red (633nm)" current=0.030A package="5 mm [THT]"]

nets:
  GND: 3S_LiPo.V-, ESC_2.Pin_6, ESC_1.Pin_6, Arduino_Mega.GND, microSD.GND, U1.IP-, U1.GND, ESP.pin2, ESP.pin_29, LED_red.cathode, LED_green.cathode, LED_blue.cathode
  11.1V: 3S_LiPo.V+, ESC_2.Pin_2, ESC_1.Pin_2
  current_input: ESC_2.Pin_1, ESC_1.Pin_1, U1.IP+
  N1: ESC_2.Pin_3, Thruster_right.gnd
  N2: ESC_2.Pin_4, Thruster_right.pulse
  N3: ESC_2.Pin_5, Thruster_right.vcc
  V_OUT: ESC_2.Pin_7, ESC_1.Pin_7, Arduino_Mega.VIN, microSD.VCC, U1.VCC, ESP.pin_30
  T2_: ESC_2.Pin_8, Arduino_Mega.D5_PWM
  N4: ESC_1.Pin_3, Thruster_left.gnd
  N5: ESC_1.Pin_4, Thruster_left.pulse
  N6: ESC_1.Pin_5, Thruster_left.vcc
  T1_: ESC_1.Pin_8, Arduino_Mega.D4_PWM
  C_OUT: Arduino_Mega.A0, U1.VOUT
  esp_write: Arduino_Mega.D17_PWM/RX2, ESP.pin4
  ESP_read: Arduino_Mega.D16_PWM/TX2, ESP.pin3
  LED_green: Arduino_Mega.D13_PWM, LED_green.anode
  LED_blue: Arduino_Mega.D12_PWM, LED_blue.anode
  LED_red: Arduino_Mega.D11_PWM, LED_red.anode
  MISO: Arduino_Mega.D50, microSD.MISO
  MOSI: Arduino_Mega.D51, microSD.MOSI
  SCK: Arduino_Mega.D52, microSD.SCK
  CS: Arduino_Mega.D53, microSD.CS

custom parts:
  Littlebee 30A ESC: LittleBee 30A 2-4 LiPo Battery ESC Brushless Speed Controller for RC FPV Multicopter.
